# Fritzing sketch PCB_design (saved by Fritzing 0.9.3b)
circuit board: 9.906cm x 7.62cm

parts:
  CZ2 = Pushbutton [package="[SMD]"]
  Phase = Pushbutton [package="[SMD]"]
  Z = Pushbutton [package="[SMD]"]
  Hadamard = Pushbutton [package="[SMD]"]
  CZ1 = Pushbutton [package="[SMD]"]
  Measure = Pushbutton [package="[SMD]"]
  U2 = RJ45 Jack [package=rj45-8]
  U1 = RJ45 Jack [package=rj45-8]
  ATTiny4313 = ATTiny4313 [chip_label=IC package=SO(w)]
  LED0 = Blue smd LED [package="0603 [SMD]"]
  LED1 = Blue smd LED [package="0603 [SMD]"]
  LED2 = Blue smd LED [package="0603 [SMD]"]
  LEDA = Blue smd LED [package="0603 [SMD]"]
  R1 = 220 Ω Resistor [package="0603 [SMD]"]
  R2 = 220 Ω Resistor [package="0603 [SMD]"]
  R3 = 220 Ω Resistor [package="0603 [SMD]"]
  R5 = 220 Ω Resistor [package="0603 [SMD]"]
  C1 = New Capacitor [part_number=CL10F104ZO8NNNC package="0603 [SMD, multilayer]"]
  BAT = Battery Holders [package=battcom_20mm_pth]
  R4 = 220 Ω Resistor [package="0603 [SMD]"]
  R6 = 220 Ω Resistor [package="0603 [SMD]"]
  LED4 = Blue smd LED [package="0603 [SMD]"]  # not connected
  C2 = New Capacitor [part_number=CL10F104ZO8NNNC package="0603 [SMD, multilayer]"]  # not connected

nets:
  N1: CZ2.Pin_1, CZ2.Pin_2, ATTiny4313.9
  N2: CZ2.Pin_3, CZ2.Pin_4, Phase.Pin_3, Phase.Pin_4, Z.Pin_3, Z.Pin_4, Hadamard.Pin_1, Hadamard.Pin_2, CZ1.Pin_1, CZ1.Pin_2, Measure.Pin_3, Measure.Pin_4, ATTiny4313.10, R1.Pin_0, R2.Pin_1, C1.0, BAT.-
  N3: Phase.Pin_1, Phase.Pin_2, ATTiny4313.8
  N4: Z.Pin_1, Z.Pin_2, ATTiny4313.7
  N5: Hadamard.Pin_3, Hadamard.Pin_4, ATTiny4313.6
  N6: CZ1.Pin_3, CZ1.Pin_4, ATTiny4313.2
  N7: Measure.Pin_1, Measure.Pin_2, ATTiny4313.11
  N8: U2.1, ATTiny4313.3
  N9: U2.2, ATTiny4313.1
  N10: U2.3, R5.Pin_0
  N11: U2.4, ATTiny4313.20, C1.1, BAT.+
  N12: U2.5, ATTiny4313.17
  N13: U2.6, ATTiny4313.19
  N14: U2.8, ATTiny4313.18
  N15: U1.1, ATTiny4313.12
  N16: U1.3, R4.Pin_1
  N17: ATTiny4313.4, R6.Pin_1
  N18: ATTiny4313.5, R3.Pin_0
  N19: ATTiny4313.13, LEDA.anode
  N20: ATTiny4313.14, LED2.anode
  N21: ATTiny4313.15, LED1.anode
  N22: ATTiny4313.16, LED0.anode
  N23: LED0.cathode, LED1.cathode, LED2.cathode, R1.Pin_1
  N24: LEDA.cathode, R2.Pin_0
  N25: R3.Pin_1, R4.Pin_0
  N26: R5.Pin_1, R6.Pin_0

notes:
  J2
  J1
  +
  -

custom parts:
  Pushbutton: A generic pushbutton.
  Blue smd LED: A generic blue LED (~1.8V)
  220 Ω Resistor: A generic resistor (0.25W)
  New Capacitor: 0.01 nF multilayered Ceramic Capacitor
  Battery Holders: Battery Holders Various common sizes : AA, AAA, 20mm coin cell and 12mm coin cell.
  Blue smd LED: A generic blue LED (~1.8V)
