# Fritzing sketch circuit (saved by Fritzing 0.9.3b)
stripboards: 1

parts:
  IC1 = IC, DIP package, 20 pins [chip_label=ATtiny261A]
  VCC1 = Battery
  S1 = Pushbutton [package="[THT]"]
  S2 = Pushbutton [package="[THT]"]
  S3 = Pushbutton [package="[THT]"]
  S4 = Pushbutton [package="[THT]"]
  S5 = Pushbutton [package="[THT]"]
  LED2 = LED - 3mm [color="Red (633nm)" package="3 mm [THT]"]
  LED3 = LED - 3mm [color="Green (555nm)" package="3 mm [THT]"]
  C1 = Ceramic Capacitor [capacitance=100nF package="100 mil [THT, multilayer]"]
  TRS2 = Stereo Jack (TRS) 3.5mm [package="PG203J [THT]"]
  TRS3 = Stereo Jack (TRS) 3.5mm [package="PG203J [THT]"]
  J1 = male pin header, 6 pins [form="♂ (male)"]
  LED4 = LED - 3mm [color="Red (633nm)" package="3 mm [THT]"]
  R4 = Resistor [tolerance=±5% resistance=220 package=THT]

nets:
  N1: IC1.pin1, J1.pin4
  N2: IC1.pin2, J1.pin5
  N3: IC1.pin3, J1.pin6
  N4: IC1.pin4, TRS3.Ring
  N5: IC1.pin5, VCC1.+, C1.0, J1.pin2
  N6: IC1.pin6, VCC1.-, S1.Pin_3, S1.Pin_4, S2.Pin_1, S2.Pin_2, S3.Pin_3, S3.Pin_4, S4.Pin_1, S4.Pin_2, S5.Pin_1, S5.Pin_2, C1.1, TRS2.Sleeve, TRS3.Sleeve, J1.pin1, R4.Pin_0
  N7: IC1.pin7, TRS3.Tip
  N8: IC1.pin8, S4.Pin_3, S4.Pin_4
  N9: IC1.pin9, S1.Pin_1, S1.Pin_2
  N10: IC1.pin10, J1.pin3
  N11: IC1.pin11, TRS2.Tip
  N12: IC1.pin12, TRS2.Ring
  N13: IC1.pin13, S2.Pin_3, S2.Pin_4
  N14: IC1.pin14, LED3.anode
  N15: IC1.pin17, LED2.cathode
  N16: IC1.pin18, LED4.cathode
  N17: IC1.pin19, S3.Pin_1, S3.Pin_2
  N18: IC1.pin20, S5.Pin_3, S5.Pin_4
  N19: LED2.anode, LED3.cathode, LED4.anode, R4.Pin_1

custom parts:
  Stereo Jack (TRS) 3.5mm: Stereo Jack 3.5mm
